// Logisim project MCU.circ as structural Verilog: 1 circuit, main circuit main
module main (
  input  in_1,
  input  in_2,
  input  in_3,
  input  A,
  input  in_5,
  input  in_6,
  input  B,
  input  in_8,
  input  SUB,
  input  in_10,
  input  in_11,
  input  in_12,
  input  in_13,
  input  in_14,
  input  in_15,
  input  in_16,
  input  in_17,
  input  S0,
  input  S1
);

  wire and_1_out, and_2_out, and_3_out, and_4_out, and_5_out, and_6_out, and_9_out, and_10_out, and_11_out,
       and_14_out, and_15_out, and_16_out, and_19_out, and_20_out, and_21_out, and_22_out, and_23_out,
       and_24_out, and_27_out, and_28_out, and_29_out, and_30_out, and_31_out, and_32_out, and_33_out,
       and_34_out, and_35_out, and_36_out, and_37_out, and_38_out, and_39_out, and_40_out, and_41_out,
       and_42_out, and_43_out, and_44_out, and_45_out, and_46_out, and_47_out, and_48_out, and_49_out,
       and_50_out, and_51_out, and_52_out, and_53_out, and_54_out, and_55_out, and_56_out, and_57_out,
       and_58_out, and_59_out, and_60_out, and_61_out, and_62_out, and_63_out, and_64_out, and_65_out,
       and_66_out, and_67_out, and_68_out, and_69_out, and_70_out, and_71_out, and_72_out, and_73_out,
       and_74_out, and_75_out, and_76_out, and_77_out, and_78_out, and_79_out, and_80_out, and_81_out,
       and_82_out, and_83_out, and_84_out, and_85_out, and_86_out, and_87_out, and_88_out, and_89_out,
       and_90_out, and_91_out, and_92_out, and_93_out, and_94_out, and_95_out, and_96_out, I0, I1, I2, I3,
       I10, I11, I12, I13, I20, I21, I22, I23, I30, I31, I32, I33, I40, I41, I42, I43, I50, I51, I52, I53,
       I60, I61, I62, I63, I70, I71, I72, I73, not_1_out, not_2_out, not_3_out, not_4_out, not_5_out,
       not_6_out, not_7_out, not_8_out, not_9_out, not_10_out, not_11_out, not_12_out, not_13_out,
       not_14_out, not_15_out, not_16_out, or_3_out, or_4_out, or_5_out, or_6_out, or_9_out, or_12_out,
       or_13_out, or_14_out, or_17_out, or_18_out, or_19_out, or_20_out, or_21_out, or_22_out, or_23_out,
       or_24_out, or_25_out, or_26_out, or_27_out, or_28_out, or_29_out, or_30_out, or_31_out, or_32_out,
       or_33_out, or_34_out, or_35_out, or_36_out, or_37_out, or_38_out, or_39_out, or_40_out, or_41_out,
       or_42_out, or_43_out, or_44_out, or_45_out, or_46_out, or_47_out, or_48_out, xor_1_out, xor_2_out,
       xor_3_out, xor_4_out, xor_7_out, xor_8_out, xor_9_out, xor_10_out, xor_13_out, xor_14_out, xor_15_out,
       xor_16_out, xor_19_out, xor_20_out, xor_21_out, xor_22_out;

  xor xor_1 (xor_1_out, B, SUB);
  xor xor_2 (xor_2_out, in_16, SUB);
  xor xor_3 (xor_3_out, A, xor_1_out);
  xor xor_4 (xor_4_out, in_14, xor_2_out);
  and and_1 (and_1_out, A, xor_1_out);
  and and_2 (and_2_out, A, SUB);
  and and_3 (and_3_out, xor_1_out, SUB);
  or or_1 (I2, A, B);
  or or_2 (I42, in_14, in_16);
  xor xor_5 (I0, xor_3_out, SUB);
  and and_4 (and_4_out, in_14, xor_2_out);
  and and_5 (and_5_out, in_14, or_22_out);
  and and_6 (and_6_out, xor_2_out, or_22_out);
  LED led_1 (.in(I2));
  LED led_2 (.in(I42));
  LED led_3 (.in(I0));
  or or_3 (or_3_out, and_1_out, and_2_out);
  xor xor_6 (I40, xor_4_out, or_22_out);
  LED led_4 (.in(I40));
  or or_4 (or_4_out, and_4_out, and_5_out);
  or or_5 (or_5_out, or_3_out, and_3_out);
  and and_7 (I1, A, B);
  LED led_5 (.in(I1));
  and and_8 (I41, in_14, in_16);
  xor xor_7 (xor_7_out, in_8, SUB);
  or or_6 (or_6_out, or_4_out, and_6_out);
  LED led_6 (.in(I41));
  xor xor_8 (xor_8_out, in_17, SUB);
  or or_7 (I12, in_5, in_8);
  or or_8 (I52, in_15, in_17);
  LED led_7 (.in(I12));
  LED led_8 (.in(I52));
  xor xor_9 (xor_9_out, in_5, xor_7_out);
  and and_9 (and_9_out, in_5, xor_7_out);
  and and_10 (and_10_out, in_5, or_5_out);
  and and_11 (and_11_out, xor_7_out, or_5_out);
  xor xor_10 (xor_10_out, in_15, xor_8_out);
  and and_12 (I11, in_5, in_8);
  LED led_9 (.in(I11));
  and and_13 (I51, in_15, in_17);
  xor xor_11 (I10, xor_9_out, or_5_out);
  and and_14 (and_14_out, in_15, xor_8_out);
  and and_15 (and_15_out, in_15, or_6_out);
  LED led_10 (.in(I51));
  LED led_11 (.in(I10));
  or or_9 (or_9_out, and_9_out, and_10_out);
  and and_16 (and_16_out, xor_8_out, or_6_out);
  or or_10 (I22, in_2, in_6);
  or or_11 (I62, in_10, in_12);
  xor xor_12 (I50, xor_10_out, or_6_out);
  LED led_12 (.in(I50));
  or or_12 (or_12_out, and_14_out, and_15_out);
  LED led_13 (.in(I22));
  LED led_14 (.in(I62));
  or or_13 (or_13_out, or_9_out, and_11_out);
  xor xor_13 (xor_13_out, in_6, SUB);
  or or_14 (or_14_out, or_12_out, and_16_out);
  xor xor_14 (xor_14_out, in_12, SUB);
  and and_17 (I21, in_2, in_6);
  LED led_15 (.in(I21));
  and and_18 (I61, in_10, in_12);
  LED led_16 (.in(I61));
  or or_15 (I32, in_1, in_3);
  or or_16 (I72, in_11, in_13);
  LED led_17 (.in(I32));
  LED led_18 (.in(I72));
  xor xor_15 (xor_15_out, in_2, xor_13_out);
  and and_19 (and_19_out, in_2, xor_13_out);
  and and_20 (and_20_out, in_2, or_13_out);
  and and_21 (and_21_out, xor_13_out, or_13_out);
  xor xor_16 (xor_16_out, in_10, xor_14_out);
  xor xor_17 (I20, xor_15_out, or_13_out);
  and and_22 (and_22_out, in_10, xor_14_out);
  and and_23 (and_23_out, in_10, or_14_out);
  and and_24 (and_24_out, xor_14_out, or_14_out);
  LED led_19 (.in(I20));
  or or_17 (or_17_out, and_19_out, and_20_out);
  and and_25 (I31, in_14, in_3);
  and and_26 (I71, in_11, in_13);
  or or_18 (or_18_out, or_17_out, and_21_out);
  xor xor_18 (I60, xor_16_out, or_14_out);
  LED led_20 (.in(I60));
  or or_19 (or_19_out, and_22_out, and_23_out);
  LED led_21 (.in(I31));
  LED led_22 (.in(I71));
  xor xor_19 (xor_19_out, in_3, SUB);
  or or_20 (or_20_out, or_19_out, and_24_out);
  xor xor_20 (xor_20_out, in_13, SUB);
  xor xor_21 (xor_21_out, in_1, xor_19_out);
  and and_27 (and_27_out, in_1, xor_19_out);
  and and_28 (and_28_out, in_1, or_18_out);
  and and_29 (and_29_out, xor_19_out, or_18_out);
  xor xor_22 (xor_22_out, in_11, xor_20_out);
  xor xor_23 (I30, xor_21_out, or_18_out);
  and and_30 (and_30_out, in_11, xor_20_out);
  and and_31 (and_31_out, in_11, or_20_out);
  and and_32 (and_32_out, xor_20_out, or_20_out);
  LED led_23 (.in(I30));
  or or_21 (or_21_out, and_27_out, and_28_out);
  xor xor_24 (I70, xor_22_out, or_20_out);
  or or_22 (or_22_out, or_21_out, and_29_out);
  LED led_24 (.in(I70));
  or or_23 (or_23_out, and_30_out, and_31_out);
  or or_24 (or_24_out, or_23_out, and_32_out);
  LED led_25 (.in(or_24_out));
  not not_1 (not_1_out, S0);
  not not_2 (not_2_out, S1);
  not not_3 (not_3_out, S0);
  not not_4 (not_4_out, S1);
  and and_33 (and_33_out, I40, not_1_out);
  and and_34 (and_34_out, I41, not_1_out);
  and and_35 (and_35_out, I42, S0);
  and and_36 (and_36_out, I43, S0);
  and and_37 (and_37_out, and_33_out, not_2_out);
  and and_38 (and_38_out, and_34_out, S1);
  and and_39 (and_39_out, and_35_out, not_2_out);
  and and_40 (and_40_out, and_36_out, S1);
  and and_41 (and_41_out, I0, not_3_out);
  and and_42 (and_42_out, I1, not_3_out);
  and and_43 (and_43_out, I2, S0);
  and and_44 (and_44_out, I3, S0);
  and and_45 (and_45_out, and_43_out, not_4_out);
  and and_46 (and_46_out, and_44_out, S1);
  and and_47 (and_47_out, and_41_out, not_4_out);
  and and_48 (and_48_out, and_42_out, S1);
  or or_25 (or_25_out, and_37_out, and_38_out);
  or or_26 (or_26_out, and_39_out, and_40_out);
  or or_27 (or_27_out, and_47_out, and_48_out);
  or or_28 (or_28_out, and_45_out, and_46_out);
  or or_29 (or_29_out, or_25_out, or_26_out);
  LED led_26 (.in(or_29_out));
  or or_30 (or_30_out, or_27_out, or_28_out);
  LED led_27 (.in(or_30_out));
  not not_5 (not_5_out, S0);
  not not_6 (not_6_out, S1);
  and and_49 (and_49_out, I51, not_5_out);
  and and_50 (and_50_out, I52, S0);
  and and_51 (and_51_out, I53, S0);
  not not_7 (not_7_out, S0);
  not not_8 (not_8_out, S1);
  and and_52 (and_52_out, I50, not_5_out);
  and and_53 (and_53_out, and_52_out, not_6_out);
  and and_54 (and_54_out, and_49_out, S1);
  and and_55 (and_55_out, and_50_out, not_6_out);
  and and_56 (and_56_out, and_51_out, S1);
  and and_57 (and_57_out, I10, not_7_out);
  and and_58 (and_58_out, I11, not_7_out);
  and and_59 (and_59_out, I12, S0);
  and and_60 (and_60_out, I13, S0);
  and and_61 (and_61_out, and_57_out, not_8_out);
  and and_62 (and_62_out, and_58_out, S1);
  and and_63 (and_63_out, and_59_out, not_8_out);
  and and_64 (and_64_out, and_60_out, S1);
  or or_31 (or_31_out, and_53_out, and_54_out);
  or or_32 (or_32_out, and_55_out, and_56_out);
  or or_33 (or_33_out, and_61_out, and_62_out);
  or or_34 (or_34_out, and_63_out, and_64_out);
  or or_35 (or_35_out, or_31_out, or_32_out);
  LED led_28 (.in(or_35_out));
  or or_36 (or_36_out, or_33_out, or_34_out);
  LED led_29 (.in(or_36_out));
  not not_9 (not_9_out, S0);
  not not_10 (not_10_out, S1);
  not not_11 (not_11_out, S0);
  not not_12 (not_12_out, S1);
  and and_65 (and_65_out, I60, not_9_out);
  and and_66 (and_66_out, I61, not_9_out);
  and and_67 (and_67_out, I62, S0);
  and and_68 (and_68_out, I63, S0);
  and and_69 (and_69_out, and_67_out, not_10_out);
  and and_70 (and_70_out, and_68_out, S1);
  and and_71 (and_71_out, I21, not_11_out);
  and and_72 (and_72_out, I22, S0);
  and and_73 (and_73_out, I23, S0);
  and and_74 (and_74_out, and_65_out, not_10_out);
  and and_75 (and_75_out, and_66_out, S1);
  and and_76 (and_76_out, I20, not_11_out);
  and and_77 (and_77_out, and_76_out, not_12_out);
  and and_78 (and_78_out, and_71_out, S1);
  and and_79 (and_79_out, and_72_out, not_12_out);
  and and_80 (and_80_out, and_73_out, S1);
  or or_37 (or_37_out, and_74_out, and_75_out);
  or or_38 (or_38_out, and_69_out, and_70_out);
  or or_39 (or_39_out, and_77_out, and_78_out);
  or or_40 (or_40_out, and_79_out, and_80_out);
  or or_41 (or_41_out, or_37_out, or_38_out);
  LED led_30 (.in(or_41_out));
  or or_42 (or_42_out, or_39_out, or_40_out);
  LED led_31 (.in(or_42_out));
  not not_13 (not_13_out, S0);
  not not_14 (not_14_out, S1);
  not not_15 (not_15_out, S0);
  not not_16 (not_16_out, S1);
  and and_81 (and_81_out, I70, not_13_out);
  and and_82 (and_82_out, I71, not_13_out);
  and and_83 (and_83_out, I72, S0);
  and and_84 (and_84_out, I73, S0);
  and and_85 (and_85_out, and_84_out, S1);
  and and_86 (and_86_out, I32, S0);
  and and_87 (and_87_out, I33, S0);
  and and_88 (and_88_out, and_81_out, not_14_out);
  and and_89 (and_89_out, and_82_out, S1);
  and and_90 (and_90_out, and_83_out, not_14_out);
  and and_91 (and_91_out, I30, not_15_out);
  and and_92 (and_92_out, I31, not_15_out);
  and and_93 (and_93_out, and_91_out, not_16_out);
  and and_94 (and_94_out, and_92_out, S1);
  and and_95 (and_95_out, and_86_out, not_16_out);
  and and_96 (and_96_out, and_87_out, S1);
  or or_43 (or_43_out, and_88_out, and_89_out);
  or or_44 (or_44_out, and_90_out, and_85_out);
  or or_45 (or_45_out, and_93_out, and_94_out);
  or or_46 (or_46_out, and_95_out, and_96_out);
  or or_47 (or_47_out, or_43_out, or_44_out);
  LED led_32 (.in(or_47_out));
  or or_48 (or_48_out, or_45_out, or_46_out);
  LED led_33 (.in(or_48_out));

  // Other names for the same wires on the sheet: A0 = A; A1 = in_5; A2 = in_2; A3 = in_1; A4 = in_14; A5 = in_15;
  //   A6 = in_10; A7 = in_11; B0 = B; B1 = in_8; B2 = in_6; B3 = in_3; B4 = in_16; B5 = in_17; B6 = in_12; B7 = in_13

  // Notes on the sheet:
  //   OR GATE UNIT
  //   AND GATE UNIT
  //   Full Adder 8-bit & SUB 8-bit circuits
  //   LOGIC UNITS CIRCUITS
  //   ALU Circuits
  //   MUX Circuits
endmodule
